// Logisim project s-mips.circ as structural Verilog: 9 circuits, main circuit S-MIPS Board
module S_MIPS_Board (
  input  DESHABILITAR_DISPATCHER,
  output halt
);

  wire button_1_out, CLK, CS, d_ff_1_q, LCLR, LoadRAM, LoadRAMOn, LW, R_R_W, R_W, ram_dispatcher_1_finished,
       RCS, Reset_out, RST, TTY_EN;
  wire [2:0] KDB;
  wire [3:0] LMask, Mask, ram_1_read_time, ram_1_write_time, RMask;
  wire [6:0] KDB_DATA, TTY_DATA;
  wire [15:0] Addr, LAddr, RAddr;
  wire [31:0] I0, I1, I2, I3, LData, ram_1_data_out_0, ram_1_data_out_1, ram_1_data_out_2, ram_1_data_out_3,
       RI0, RI1, RI2, RI3;

  TTY #(.rows(25), .cols(80)) tty_1 (.data(TTY_DATA), .clk(CLK), .we(TTY_EN), .clr(RST));
  not not_1 (LoadRAMOn, ram_dispatcher_1_finished);
  RAM_Dispatcher ram_dispatcher_1 (
    .WriteTime(ram_1_write_time), .Clock(CLK), .Data(LData), .Address(LAddr), .Mask(LMask),
    .Finished(ram_dispatcher_1_finished), .Write(LW), .CLR(LCLR));
  Keyboard #(.buflen(64)) keyboard_1 (.clk(CLK), .re(KDB[0]), .avail(KDB[2]), .data(KDB_DATA));  // open: clr
  RAM ram_1 (
    .Address(RAddr), .Data_Out_0(ram_1_data_out_0), .Data_Out_1(ram_1_data_out_1),
    .Data_Out_2(ram_1_data_out_2), .Data_Out_3(ram_1_data_out_3), .Data_In_0(RI0), .Data_In_1(RI1),
    .Data_In_2(RI2), .Data_In_3(RI3), .Mask(RMask), .nRead_Write(R_R_W), .Chip_Select(RCS),
    .Read_Time(ram_1_read_time), .Reset(button_1_out), .Write_Time(ram_1_write_time));
  Button button_1 (.out(button_1_out));
  D_Flip_Flop d_ff_1 (.clk(CLK), .D(1'b1), .Q(d_ff_1_q), .reset(Reset_out));  // open: Qn, preset, en
  Button Reset (.out(Reset_out));
  S_MIPS s_mips_1 (
    .Kbd_Enable(KDB[0]), .Address(Addr), .Kbd_Clear(KDB[1]), .Kbd_Available(KDB[2]), .RAM_In_0(I0),
    .Kbd_ASCII_Data(KDB_DATA), .RAM_In_1(I1), .TTY_Enable(TTY_EN), .RAM_In_2(I2), .RAM_In_3(I3),
    .TTY_ASCII_Data(TTY_DATA), .Reset(RST), .RAM_Out_0(ram_1_data_out_0), .Clock(CLK),
    .RAM_Out_1(ram_1_data_out_1), .Stop(halt), .RAM_Out_2(ram_1_data_out_2), .RAM_Out_3(ram_1_data_out_3),
    .Mask(Mask), .Read_Time(ram_1_read_time), .Write_Time(ram_1_write_time), .nRead_Write(R_W),
    .Chip_Select(CS));
  D_Flip_Flop d_ff_2 (.clk(CLK), .D(d_ff_1_q), .Qn(LCLR), .reset(Reset_out));  // open: Q, preset, en
  or or_1 (RST, LCLR, LoadRAM);
  Clock clock_1 (.out(CLK));
  Multiplexer #(.width(32), .enable("false")) multiplexer_1 (.in0(I0), .in1(LData), .out(RI0), .sel(LoadRAM));
  Multiplexer #(.width(32), .enable("false")) multiplexer_2 (.in0(I1), .in1(LData), .out(RI1), .sel(LoadRAM));
  Multiplexer #(.width(32), .enable("false")) multiplexer_3 (.in0(I2), .in1(LData), .out(RI2), .sel(LoadRAM));
  Multiplexer #(.width(32), .enable("false")) multiplexer_4 (.in0(I3), .in1(LData), .out(RI3), .sel(LoadRAM));
  and and_1 (LoadRAM, ~DESHABILITAR_DISPATCHER, LoadRAMOn);  // AND_Gate
  Multiplexer #(.width(16), .enable("false")) multiplexer_5 (.in0(Addr), .in1(LAddr), .out(RAddr), .sel(LoadRAM));
  Multiplexer #(.width(4), .enable("false")) multiplexer_6 (.in0(Mask), .in1(LMask), .out(RMask), .sel(LoadRAM));
  Multiplexer #(.enable("false")) multiplexer_7 (.in0(CS), .in1(LW), .out(RCS), .sel(LoadRAM));
  Multiplexer #(.enable("false")) multiplexer_8 (.in0(R_W), .in1(LW), .out(R_R_W), .sel(LoadRAM));

  // Notes on the sheet:
  //   NO MODIFICAR
  //   Keyboard
endmodule

module RAM (
  input  [15:0] Address,
  input  [31:0] Data_In_0,
  input  [31:0] Data_In_1,
  input  [31:0] Data_In_2,
  input  [31:0] Data_In_3,
  input  [3:0] Mask,
  input  nRead_Write,
  input  Chip_Select,
  input  Reset,
  output [31:0] Data_Out_0,
  output [31:0] Data_Out_1,
  output [31:0] Data_Out_2,
  output [31:0] Data_Out_3,
  output [3:0] Read_Time,
  output [3:0] Write_Time
);

  wire and_2_out, and_3_out, and_4_out, and_5_out, and_6_out, and_7_out, and_8_out, and_9_out, Changed, CLK,
       comparator_2_eq, comparator_3_eq, comparator_4_eq, comparator_5_eq, comparator_6_eq, Count,
       demultiplexer_3_out0, Idle, Idle_q, Load, Load0, Load1, nand_1_out, or_1_out, or_2_out, or_3_out,
       or_4_out, or_5_out, or_6_out, or_7_out, or_8_out, or_9_out, or_10_out, Proc_q, Update_Mem, Zero_Time;
  wire [3:0] counter_1_q, multiplexer_1_out, subtractor_1_out;
  wire [31:0] register_1_q, register_2_q, register_3_q, register_4_q, register_5_q;

  // Probe on 4'b0011
  // Probe on 4'b0010
  Multiplexer #(.width(4), .enable("false")) multiplexer_1 (
    .in0(4'b0011), .in1(4'b0010), .out(multiplexer_1_out), .sel(nRead_Write));
  or or_1 (or_1_out, Idle, Update_Mem);
  or or_2 (or_2_out, ~Chip_Select, Reset);  // OR_Gate
  Subtractor #(.width(4)) subtractor_1 (.a(multiplexer_1_out), .b(4'b0010), .out(subtractor_1_out));  // open: bin, bout
  Demultiplexer #(.enable("false")) demultiplexer_1 (.out0(Idle), .out1(Load0), .in(Idle_q), .sel(Changed));
  D_Flip_Flop u_Idle (.clk(CLK), .D(or_1_out), .Q(Idle_q), .preset(or_2_out));  // open: Qn, en, reset
  // Probe on counter_1_q
  Counter #(.width(4), .max('hf)) counter_1 (
    .load(Load), .D(subtractor_1_out), .count(Count), .Q(counter_1_q), .clk(CLK), .clr(or_3_out));  // open: carry
  or or_3 (or_3_out, ~Chip_Select, Reset);  // OR_Gate
  Comparator #(.width(4), .mode("unsigned")) comparator_1 (
    .a(4'b0000), .b(counter_1_q), .eq(Zero_Time));  // open: gt, lt
  or or_4 (or_4_out, Count, Load0, Load1);
  Register #(.width(32)) register_1 (.D(Data_In_0), .en(Chip_Select), .Q(register_1_q), .clk(CLK), .clr(or_5_out));
  or or_5 (or_5_out, ~Chip_Select, Reset);  // OR_Gate
  Register #(.width(32)) register_2 (.D(Data_In_1), .en(Chip_Select), .Q(register_2_q), .clk(CLK), .clr(or_6_out));
  or or_6 (or_6_out, ~Chip_Select, Reset);  // OR_Gate
  Register #(.width(32)) register_3 (.D(Data_In_2), .en(Chip_Select), .Q(register_3_q), .clk(CLK), .clr(or_7_out));
  or or_7 (or_7_out, ~Chip_Select, Reset);  // OR_Gate
  Register #(.width(32)) register_4 (.D(Data_In_3), .en(Chip_Select), .Q(register_4_q), .clk(CLK), .clr(or_8_out));
  or or_8 (or_8_out, ~Chip_Select, Reset);  // OR_Gate
  Register #(.width(32)) register_5 (
    .D({{11{1'b1}}, nRead_Write, Mask, Address}), .en(Chip_Select), .Q(register_5_q), .clk(CLK),
    .clr(or_9_out));
  or or_9 (or_9_out, ~Chip_Select, Reset);  // OR_Gate
  D_Flip_Flop Proc (.clk(CLK), .D(or_4_out), .Q(Proc_q), .reset(or_10_out));  // open: Qn, preset, en
  or or_10 (or_10_out, ~Chip_Select, Reset);  // OR_Gate
  Demultiplexer #(.enable("false")) demultiplexer_2 (
    .out0(Count), .out1(Update_Mem), .in(demultiplexer_3_out0), .sel(Zero_Time));
  Demultiplexer #(.enable("false")) demultiplexer_3 (
    .out0(demultiplexer_3_out0), .out1(Load1), .in(Proc_q), .sel(Changed));
  Clock clock_1 (.out(CLK));
  Comparator #(.width(32)) comparator_2 (.a(register_1_q), .b(Data_In_0), .eq(comparator_2_eq));  // open: gt, lt
  Comparator #(.width(32)) comparator_3 (.a(register_2_q), .b(Data_In_1), .eq(comparator_3_eq));  // open: gt, lt
  Comparator #(.width(32)) comparator_4 (.a(register_3_q), .b(Data_In_2), .eq(comparator_4_eq));  // open: gt, lt
  Comparator #(.width(32)) comparator_5 (.a(register_4_q), .b(Data_In_3), .eq(comparator_5_eq));  // open: gt, lt
  Comparator #(.width(32)) comparator_6 (
    .a(register_5_q), .b({{11{1'b1}}, nRead_Write, Mask, Address}), .eq(comparator_6_eq));  // open: gt, lt
  nand nand_1 (nand_1_out, comparator_6_eq, comparator_2_eq, comparator_3_eq, comparator_4_eq, comparator_5_eq);
  and and_1 (Changed, nand_1_out, Chip_Select);
  or or_11 (Load, Count, Load1, Load0);
  and and_2 (and_2_out, Mask[0], Update_Mem, nRead_Write);
  and and_3 (and_3_out, Mask[1], Update_Mem, nRead_Write);
  and and_4 (and_4_out, Mask[2], Update_Mem, nRead_Write);
  and and_5 (and_5_out, Mask[3], Update_Mem, nRead_Write);
  RAM_part #(.addrWidth(16), .dataWidth(32), .bus("separate")) ram_1 (
    .addr(Address), .din(Data_In_0), .data(Data_Out_0), .str(and_2_out), .sel(Chip_Select), .clk(CLK),
    .ld(and_6_out), .clr(Reset));
  and and_6 (and_6_out, ~nRead_Write, Idle);  // AND_Gate
  RAM_part #(.addrWidth(16), .dataWidth(32), .bus("separate")) ram_2 (
    .addr(Address), .din(Data_In_1), .data(Data_Out_1), .str(and_3_out), .sel(Chip_Select), .clk(CLK),
    .ld(and_7_out), .clr(Reset));
  and and_7 (and_7_out, ~nRead_Write, Idle);  // AND_Gate
  RAM_part #(.addrWidth(16), .dataWidth(32), .bus("separate")) ram_3 (
    .addr(Address), .din(Data_In_2), .data(Data_Out_2), .str(and_4_out), .sel(Chip_Select), .clk(CLK),
    .ld(and_8_out), .clr(Reset));
  and and_8 (and_8_out, ~nRead_Write, Idle);  // AND_Gate
  RAM_part #(.addrWidth(16), .dataWidth(32), .bus("separate")) ram_4 (
    .addr(Address), .din(Data_In_3), .data(Data_Out_3), .str(and_5_out), .sel(Chip_Select), .clk(CLK),
    .ld(and_9_out), .clr(Reset));
  and and_9 (and_9_out, ~nRead_Write, Idle);  // AND_Gate

  assign Read_Time = 4'b0011;
  assign Write_Time = 4'b0010;

  // Other names for the same wires on the sheet: M0 = Mask[0]; M1 = Mask[1]; M2 = Mask[2]; M3 = Mask[3];
  //   RW = nRead_Write; CLR = Reset; CS = Chip_Select; Load2 = Count

  // Notes on the sheet:
  //   NO MODIFICAR
  //   excepto quizás los valores RT y WT
  //   BANK0
  //   BANK1
  //   BANK2
  //   BANK3
endmodule

module S_MIPS (
  input  Kbd_Available,
  input  [6:0] Kbd_ASCII_Data,
  input  [31:0] RAM_Out_0,
  input  [31:0] RAM_Out_1,
  input  Reset,
  input  [31:0] RAM_Out_2,
  input  Clock,
  input  [31:0] RAM_Out_3,
  input  [3:0] Read_Time,
  input  [3:0] Write_Time,
  output Kbd_Enable,
  output [15:0] Address,
  output Kbd_Clear,
  output TTY_Enable,
  output [6:0] TTY_ASCII_Data,
  output Stop,
  output [31:0] RAM_In_0,
  output [31:0] RAM_In_1,
  output [31:0] RAM_In_2,
  output [31:0] RAM_In_3,
  output [3:0] Mask,
  output nRead_Write,
  output Chip_Select
);


  // Other names for the same wires on the sheet: CLK = Clock; CLR = Reset; CS = Chip_Select;
  //   KBD_AVAIL = Kbd_Available; KBD_CLR = Kbd_Clear; KBD_DATA[6:0] = Kbd_ASCII_Data; RAM_A[15:0] = Address;
  //   RAM_INPUT_0[31:0] = RAM_In_0; RAM_INPUT_1[31:0] = RAM_In_1; RAM_INPUT_2[31:0] = RAM_In_2;
  //   RAM_INPUT_3[31:0] = RAM_In_3; RAM_MASK[3:0] = Mask; RAM_OUTPUT_0[31:0] = RAM_Out_0;
  //   RAM_OUTPUT_1[31:0] = RAM_Out_1; RAM_OUTPUT_2[31:0] = RAM_Out_2; RAM_OUTPUT_3[31:0] = RAM_Out_3;
  //   RW = nRead_Write; TTY_DATA[6:0] = TTY_ASCII_Data

  // Notes on the sheet:
  //   RAM ADDRESS
  //   DATA FROM RAM
  //   DATA TO RAM
  //   DATA WRITE MASK
  //   RAM TIMING
  //   RAM CONTROL
  //   KEYBOARD
  //   TTY
  //   SEQUENCING
endmodule

module RAM_Dispatcher (
  input  [3:0] WriteTime,
  input  Clock,
  input  CLR,
  output [31:0] Data,
  output [15:0] Address,
  output [3:0] Mask,
  output Finished,
  output Write
);

  wire demultiplexer_2_out1, demultiplexer_3_out1, End, IDLE_q, IncAddr, Load, or_1_out, or_2_out, While_q,
       WriteEnd;
  wire [3:0] counter_1_q;
  wire [31:0] CurrentAddress_q;

  Counter #(.width(32), .max('hffffffff)) CurrentAddress (
    .count(IncAddr), .Q({CurrentAddress_q[31:18], Address, CurrentAddress_q[1:0]}), .clk(Clock), .clr(CLR));  // open: load, D, carry
  or or_1 (or_1_out, IncAddr, demultiplexer_3_out1, Finished);
  D_Flip_Flop IDLE (.clk(Clock), .D(or_1_out), .Q(IDLE_q), .preset(CLR));  // open: Qn, en, reset
  Demultiplexer #(.enable("false")) demultiplexer_1 (.out0(Load), .out1(Finished), .in(IDLE_q), .sel(End));
  D_Flip_Flop While (.clk(Clock), .D(or_2_out), .Q(While_q), .reset(CLR));  // open: Qn, preset, en
  or or_2 (or_2_out, Write, Load);
  RAM_part #(.addrWidth(18), .dataWidth(32)) ram_1 (
    .addr({Address, CurrentAddress_q[1:0]}), .data(Data), .clk(Clock));  // open: sel, ld, clr
  Demultiplexer #(.enable("false")) demultiplexer_2 (
    .out0(Write), .out1(demultiplexer_2_out1), .in(While_q), .sel(WriteEnd));
  Decoder #(.select(2)) decoder_1 (
    .out0(Mask[0]), .out1(Mask[1]), .out2(Mask[2]), .out3(Mask[3]), .sel(CurrentAddress_q[1:0]));  // open: en
  Demultiplexer #(.enable("false")) demultiplexer_3 (
    .out0(IncAddr), .out1(demultiplexer_3_out1), .in(demultiplexer_2_out1), .sel(End));
  Counter #(.width(4), .max('hf)) counter_1 (
    .load(Load), .D(WriteTime), .count(Write), .Q(counter_1_q), .clk(Clock));  // open: carry, clr
  Comparator #(.width(32)) comparator_1 (.a(Data), .b({32{1'b1}}), .eq(End));  // open: gt, lt
  Comparator #(.width(4)) comparator_2 (.a(4'b0000), .b(counter_1_q), .eq(WriteEnd));  // open: gt, lt

  // Other names for the same wires on the sheet: CLK = Clock; Count = Write; WT[3:0] = WriteTime
endmodule

module Register_File (
  input  MD,
  input  Reset,
  input  [4:0] A,
  input  [4:0] B,
  input  [31:0] DI,
  input  RW,
  input  Clk,
  input  [4:0] DA,
  input  [31:0] HI_value,
  input  [31:0] LO_value,
  output [31:0] RA,
  output [31:0] RB,
  output [31:0] Stack_Pointer,
  output [31:0] HI_value_2,
  output [31:0] LO_value_2
);

  wire R1, R2, R3, R4, R5, R6, R7, R8, R9, R10, R11, R12, R13, R14, R15, R16, R17, R18, R19, R20, R21, R22,
       R23, R24, R25, R26, R27, R28, R29, R30, R31;
  wire [31:0] O19, OR0, OR1, OR2, OR3, OR4, OR5, OR6, OR7, OR8, OR9, OR10, OR11, OR12, OR13, OR14, OR15,
       OR16, OR17, OR18, OR19, OR20, OR21, OR22, OR23, OR24, OR25, OR26, OR27, OR28, OR29, OR30;

  Decoder #(.select(5), .disabled(0)) decoder_1 (
    .out1(R1), .out2(R2), .out3(R3), .out4(R4), .out5(R5), .out6(R6), .out7(R7), .out8(R8), .out9(R9),
    .out10(R10), .out11(R11), .out12(R12), .out13(R13), .out14(R14), .out15(R15), .out16(R16), .out17(R17),
    .out18(R18), .out19(R19), .out20(R20), .out21(R21), .out22(R22), .out23(R23), .out24(R24), .out25(R25),
    .out26(R26), .out27(R27), .out28(R28), .out29(R29), .out30(R30), .out31(R31), .sel(DA), .en(RW));  // open: out0
  Multiplexer #(.select(5), .width(32), .disabled(0), .enable("false")) multiplexer_1 (
    .in1(OR1), .in2(OR2), .in3(OR3), .in4(OR4), .in5(OR5), .in6(OR6), .in7(OR7), .in8(OR8), .in9(OR9),
    .in10(OR10), .in11(OR11), .in12(OR12), .in13(OR13), .in14(OR14), .in15(OR15), .in16(OR16), .in17(OR17),
    .in18(OR18), .in19(O19), .in20(OR20), .in21(OR21), .in22(OR22), .in23(OR23), .in24(OR24), .in25(OR25),
    .in26(OR26), .in27(OR27), .in28(OR28), .in29(OR29), .in30(OR30), .in31(Stack_Pointer), .out(RA), .sel(A));  // open: in0
  Multiplexer #(.select(5), .width(32), .disabled(0), .enable("false")) multiplexer_2 (
    .in1(OR1), .in2(OR2), .in3(OR3), .in4(OR4), .in5(OR5), .in6(OR6), .in7(OR7), .in8(OR8), .in9(OR9),
    .in10(OR10), .in11(OR11), .in12(OR12), .in13(OR13), .in14(OR14), .in15(OR15), .in16(OR16), .in17(OR17),
    .in18(OR18), .in19(O19), .in20(OR20), .in21(OR21), .in22(OR22), .in23(OR23), .in24(OR24), .in25(OR25),
    .in26(OR26), .in27(OR27), .in28(OR28), .in29(OR29), .in30(OR30), .in31(Stack_Pointer), .out(RB), .sel(B));  // open: in0
  Register #(.width(32)) register_1 (.D({32{1'b0}}), .Q(OR0), .clk(Clk), .clr(Reset));  // open: en
  Register #(.width(32)) register_2 (.D(DI), .en(R8), .Q(OR8), .clk(Clk), .clr(Reset));
  Register #(.width(32)) register_3 (.D(DI), .en(R16), .Q(OR16), .clk(Clk), .clr(Reset));
  Register #(.width(32)) register_4 (.D(DI), .en(R24), .Q(OR24), .clk(Clk), .clr(Reset));
  Register #(.width(32)) register_5 (.D(DI), .en(R1), .Q(OR1), .clk(Clk), .clr(Reset));
  Register #(.width(32)) register_6 (.D(DI), .en(R9), .Q(OR9), .clk(Clk), .clr(Reset));
  Register #(.width(32)) register_7 (.D(DI), .en(R17), .Q(OR17), .clk(Clk), .clr(Reset));
  Register #(.width(32)) register_8 (.D(DI), .en(R25), .Q(OR25), .clk(Clk), .clr(Reset));
  Register #(.width(32)) HI (.D(HI_value), .en(MD), .Q(HI_value_2), .clk(Clk), .clr(Reset));
  Register #(.width(32)) register_9 (.D(DI), .en(R2), .Q(OR2), .clk(Clk), .clr(Reset));
  Register #(.width(32)) register_10 (.D(DI), .en(R10), .Q(OR10), .clk(Clk), .clr(Reset));
  Register #(.width(32)) register_11 (.D(DI), .en(R18), .Q(OR18), .clk(Clk), .clr(Reset));
  Register #(.width(32)) register_12 (.D(DI), .en(R26), .Q(OR26), .clk(Clk), .clr(Reset));
  Register #(.width(32)) register_13 (.D(DI), .en(R3), .Q(OR3), .clk(Clk), .clr(Reset));
  Register #(.width(32)) register_14 (.D(DI), .en(R11), .Q(OR11), .clk(Clk), .clr(Reset));
  Register #(.width(32)) register_15 (.D(DI), .en(R19), .Q(OR19), .clk(Clk), .clr(Reset));
  Register #(.width(32)) register_16 (.D(DI), .en(R27), .Q(OR27), .clk(Clk), .clr(Reset));
  Register #(.width(32)) register_17 (.D(DI), .en(R4), .Q(OR4), .clk(Clk), .clr(Reset));
  Register #(.width(32)) register_18 (.D(DI), .en(R12), .Q(OR12), .clk(Clk), .clr(Reset));
  Register #(.width(32)) register_19 (.D(DI), .en(R20), .Q(OR20), .clk(Clk), .clr(Reset));
  Register #(.width(32)) register_20 (.D(DI), .en(R28), .Q(OR28), .clk(Clk), .clr(Reset));
  Register #(.width(32)) LO (.D(LO_value), .en(MD), .Q(LO_value_2), .clk(Clk), .clr(Reset));
  Register #(.width(32)) register_21 (.D(DI), .en(R5), .Q(OR5), .clk(Clk), .clr(Reset));
  Register #(.width(32)) register_22 (.D(DI), .en(R13), .Q(OR13), .clk(Clk), .clr(Reset));
  Register #(.width(32)) register_23 (.D(DI), .en(R21), .Q(OR21), .clk(Clk), .clr(Reset));
  Register #(.width(32)) register_24 (.D(DI), .en(R29), .Q(OR29), .clk(Clk), .clr(Reset));
  Register #(.width(32)) register_25 (.D(DI), .en(R6), .Q(OR6), .clk(Clk), .clr(Reset));
  Register #(.width(32)) register_26 (.D(DI), .en(R14), .Q(OR14), .clk(Clk), .clr(Reset));
  Register #(.width(32)) register_27 (.D(DI), .en(R22), .Q(OR22), .clk(Clk), .clr(Reset));
  Register #(.width(32)) register_28 (.D(DI), .en(R30), .Q(OR30), .clk(Clk), .clr(Reset));
  Register #(.width(32)) register_29 (.D(DI), .en(R7), .Q(OR7), .clk(Clk), .clr(Reset));
  Register #(.width(32)) register_30 (.D(DI), .en(R15), .Q(OR15), .clk(Clk), .clr(Reset));
  Register #(.width(32)) register_31 (.D(DI), .en(R23), .Q(OR23), .clk(Clk), .clr(Reset));
  Register #(.width(32)) register_32 (.D(DI), .en(R31), .Q(Stack_Pointer), .clk(Clk), .clr(Reset));

  // Other names for the same wires on the sheet: OR31[31:0] = Stack_Pointer
endmodule

module ALU (
  input  [31:0] A,
  input  [31:0] B
);

  wire comparator_2_lt;

  Adder #(.width(32)) adder_1 ();  // open: a, b, out, cin, cout
  Divider #(.width(1)) divider_1 ();  // open: a, b, out, upper, rem
  // OR_Gate or_1 is placed but not wired
  Subtractor #(.width(32)) subtractor_1 ();  // open: a, b, out, bin, bout
  Comparator #(.width(32)) comparator_1 ();  // open: a, b, gt, eq, lt
  // NOR_Gate nor_1 is placed but not wired
  Comparator #(.width(32)) comparator_2 (.lt(comparator_2_lt));  // open: a, b, gt, eq
  Bit_Extender #(.in_width(1), .out_width(32)) bit_extender_1 (.in(comparator_2_lt));  // open: out
  Multiplier #(.width(1)) multiplier_1 ();  // open: a, b, out, cin, cout
  // AND_Gate and_1 is placed but not wired
  // XOR_Gate xor_1 is placed but not wired
  Multiplexer #(.select(4), .width(32)) multiplexer_1 ();  // open: in0, in1, in2, in3, in4, in5, in6, in7, in8, in9, in10, in11, in12, in13, in14, in15, out, sel, en
endmodule

module PC (
  output [1:0] PC_SRC_1_0
);

  wire clk, rst;
  wire [15:0] offset;
  wire [27:0] adder_2_out;
  wire [30:0] j_adress;
  wire [31:0] bit_extender_1_out, branch_adress, multiplier_1_out, next_pc, normal_adress, pc, PC_4, undriven;

  Adder #(.width(32)) adder_1 (.a(pc), .b(32'h4), .out(normal_adress));  // open: cin, cout
  Adder #(.width(32)) adder_2 (.a(pc), .b(32'h4), .out({j_adress[3:0], adder_2_out}));  // open: cin, cout
  Register #(.width(32), .trigger("falling")) PROGRAM_COUNTER (.D(next_pc), .Q(pc), .clk(clk), .clr(rst));  // open: en
  assign bit_extender_1_out = {{16{offset[15]}}, offset};  // Bit_Extender bit_extender_1
  Multiplier #(.width(32)) multiplier_1 (.a(bit_extender_1_out), .b(32'h4), .out(multiplier_1_out));  // open: cin, cout
  Adder #(.width(32)) adder_3 (.a(PC_4), .b(multiplier_1_out), .out(branch_adress));  // open: cin, cout
  Multiplexer #(.select(2), .width(32), .enable("false")) multiplexer_1 (
    .in0(normal_adress), .in1({1'b0, j_adress[30:23], 1'b0, j_adress[21:0]}), .in2(branch_adress),
    .in3(undriven), .out(next_pc), .sel(PC_SRC_1_0));

  // Other names for the same wires on the sheet: PC_4_high[3:0] = j_adress[3:0];
  //   jump[25:0] = {j_adress[30:23], j_adress[21:4]}

  // Notes on the sheet:
  //   NEXT INSTRUCTION CALCULATOR
  //   NEXT INSTRUCTION SELECTION
endmodule

module ID (
  output [1:0] PC_SRC_1_0
);

  wire and_6_out, and_7_out, and_8_out, and_9_out, and_10_out, and_12_out, and_13_out, and_14_out,
       and_15_out, and_16_out, and_17_out, and_27_out, and_28_out, and_29_out, and_30_out, aritmethic,
       branch_taken, clk, comparator_2_eq, I, is_addi, is_and, is_andi, is_beq, is_bgtz, is_blez, is_bltz,
       is_bne, is_div, is_divu, is_lw, is_mult, is_mulu, is_nor, is_or, is_ori, is_pop, is_push, is_sub,
       is_sum, is_sw, is_xor, is_xori, J, jr, \logic , nop, nor_1_out, nor_3_out, nor_4_out, nor_5_out,
       nor_6_out, nor_7_out, nor_9_out, nor_10_out, nor_11_out, nor_12_out, not_1_out, not_3_out, not_4_out,
       R, rs_0, rs_0_t, rs__0, rs__rt, rs_rt, rst;
  wire [5:1] func_code;
  wire [31:0] pc;
  wire [31:6] inst;

  Comparator #(.width(5), .mode("unsigned")) comparator_1 (
    .a(inst[25:21]), .b({inst[20:17], inst[27]}), .eq(rs_rt));  // open: gt, lt
  Comparator #(.width(5), .mode("unsigned")) comparator_2 (
    .a(inst[25:21]), .b({5{1'b0}}), .gt(rs_0_t), .eq(comparator_2_eq), .lt(rs_0));
  not not_1 (not_1_out, inst[27]);
  nor nor_1 (nor_1_out, inst[27], inst[28]);
  Register #(.width(32)) INSTRUCTION_MEMORY (
    .D(pc), .Q({inst[31:17], inst[27], inst[15:6], func_code, func_code[1]}), .clk(clk), .clr(rst));  // open: en
  nor nor_2 (nop, inst[27], inst[31], inst[30], inst[29], inst[28], inst[27], inst[26], inst[25], inst[24], inst[23], inst[22], inst[21], inst[20], inst[19], inst[18], inst[17], inst[15], inst[14], inst[13], inst[12], inst[11], inst[10], inst[9], inst[8], inst[7], inst[6], func_code[5], func_code[4], func_code[3], func_code[2], func_code[1], func_code[1]);
  not not_2 (rs__rt, rs_rt);
  or or_1 (rs__0, comparator_2_eq, rs_0);
  nor nor_3 (nor_3_out, inst[26], inst[27]);
  and and_1 (is_beq, nor_3_out, inst[28], nor_4_out);
  and and_2 (is_bne, inst[26], inst[28], not_1_out, nor_4_out);
  not not_3 (not_3_out, inst[26]);
  and and_3 (is_blez, not_3_out, inst[27], inst[28], nor_4_out);
  and and_4 (is_bgtz, inst[26], inst[27], inst[26], nor_4_out);
  and and_5 (is_bltz, nor_1_out, nor_4_out, inst[26]);
  nor nor_4 (nor_4_out, inst[29], inst[30], inst[31]);
  and and_6 (and_6_out, is_beq, rs_rt);
  and and_7 (and_7_out, is_bne, rs__rt);
  and and_8 (and_8_out, is_bltz, rs_0);
  and and_9 (and_9_out, is_blez, rs__0);
  and and_10 (and_10_out, is_bgtz, rs_0_t);
  or or_2 (branch_taken, and_6_out, and_7_out, and_8_out, and_9_out, and_10_out);
  nor nor_5 (nor_5_out, inst[26], inst[28], inst[29], inst[30], inst[31]);
  and and_11 (J, inst[27], nor_5_out);
  nor nor_6 (nor_6_out, inst[26], inst[27], inst[28], inst[29], inst[30], inst[31]);
  nor nor_7 (nor_7_out, inst[26], inst[27], inst[28]);
  buf and_12 (and_12_out, nor_7_out);  // AND_Gate
  and and_13 (and_13_out, inst[29], inst[30], inst[31]);
  and and_14 (and_14_out, inst[26], inst[27], inst[28], inst[29], inst[30], inst[31]);
  or or_3 (R, nor_6_out, and_12_out, and_14_out);
  nor nor_8 (I, J, R);
  nor nor_9 (nor_9_out, func_code[2], func_code[5]);
  nor nor_10 (nor_10_out, inst[29], inst[30], inst[31]);
  buf and_15 (and_15_out, nor_10_out);  // AND_Gate
  nor nor_11 (nor_11_out, func_code[1], func_code[2], func_code[3], func_code[4]);
  and and_16 (and_16_out, nor_11_out, R, func_code[5]);
  and and_17 (and_17_out, func_code[3], func_code[4], nor_9_out, R);
  and and_18 (is_mult, ~func_code[1], ~func_code[1], aritmethic);  // AND_Gate
  and and_19 (is_mulu, func_code[1], ~func_code[1], aritmethic);  // AND_Gate
  and and_20 (is_div, ~func_code[1], func_code[1], aritmethic);  // AND_Gate
  and and_21 (is_divu, func_code[1], func_code[1], aritmethic);
  and and_22 (is_sub, func_code[1], func_code[5], aritmethic);
  and and_23 (is_sum, ~func_code[1], func_code[5], aritmethic);  // AND_Gate
  and and_24 (is_addi, ~func_code[1], ~func_code[1], ~func_code[2], func_code[3], ~func_code[4], ~func_code[5]);  // AND_Gate
  and and_25 (jr, and_15_out, R);
  or or_4 (aritmethic, and_16_out, and_17_out);
  or or_5 (PC_SRC_1_0[0], jr, J);
  or or_6 (PC_SRC_1_0[1], jr, branch_taken);
  and and_26 (is_xor, ~inst[26], ~inst[27], ~inst[28], inst[29], ~inst[30], inst[31]);  // AND_Gate
  and and_27 (and_27_out, func_code[2], ~func_code[3], ~func_code[4], func_code[5]);  // AND_Gate
  and and_28 (and_28_out, ~func_code[1], func_code[2], func_code[3], ~func_code[4], ~func_code[5]);  // AND_Gate
  and and_29 (and_29_out, and_27_out, R);
  and and_30 (and_30_out, and_28_out, R);
  and and_31 (is_andi, ~inst[26], ~inst[27], \logic );  // AND_Gate
  and and_32 (is_ori, ~inst[26], inst[27], \logic );  // AND_Gate
  and and_33 (is_xori, inst[26], ~inst[27], \logic );  // AND_Gate
  and and_34 (is_and, ~func_code[1], \logic , func_code[2]);  // AND_Gate
  and and_35 (is_or, ~func_code[1], func_code[1], func_code[2], \logic );  // AND_Gate
  and and_36 (is_nor, func_code[1], func_code[1], func_code[2], \logic );
  or or_7 (\logic , and_29_out, and_30_out);
  nor nor_12 (nor_12_out, func_code[1], func_code[2], func_code[3], func_code[4], func_code[5]);
  not not_4 (not_4_out, func_code[1]);
  and and_37 (is_push, nor_12_out, R, func_code[1]);
  and and_38 (is_pop, nor_12_out, R, not_4_out);
  and and_39 (is_sw, inst[26], inst[27], ~inst[28], inst[29], ~inst[30], inst[31]);  // AND_Gate
  and and_40 (is_lw, inst[26], inst[27], ~inst[28], ~inst[29], ~inst[30], inst[31]);  // AND_Gate

  // Other names for the same wires on the sheet: func_code[0] = func_code[1];
  //   inst (some bits) = {inst[27], func_code, func_code[1]};
  //   jump[25:0] = {inst[25:17], inst[27], inst[15:6], func_code, func_code[1]};
  //   offset[15:0] = {inst[15:6], func_code, func_code[1]}; rd[4:0] = inst[15:11]; rt[4:0] = {inst[20:17], inst[27]};
  //   rs[4:0] = inst[25:21]; op_code[5:0] = inst[31:26]

  // Notes on the sheet:
  //   BRANCHES
  //   INSTRUCTION TYPE
  //   ARITMETHIC
  //   JUMPS
  //   LOGIC
  //   MEMORY
endmodule

module Data_Path (
);


  // Notes on the sheet:
  //   SIGN EXTENDER
endmodule
